// Logisim project SAPDOFRED.circ as structural Verilog: 10 circuits, main circuit main
module main (
  input  in_1,
  input  in_2,
  input  CLR
);

  wire Clock_out, controlled_buffer_1_out, controlled_buffer_7_out, Controller_cp, Controller_ea,
       Controller_ep, Controller_eu, Controller_halt, Controller_nce, Controller_nei, Controller_nla,
       Controller_nlb, Controller_nli, Controller_nlm, Controller_nlo, Controller_su, not_1_out, not_2_out,
       not_3_out, not_4_out, not_5_out, not_6_out, not_7_out, not_8_out, not_9_out, not_10_out;
  wire [3:0] counter2_1_q0, MAR_y0;
  wire [7:0] ALU_f1, controlled_buffer_2_out, controlled_buffer_6_out, Ins_Reg_y0, Reg_A_y0, Reg_B_y0,
       Reg_Output_y0;

  assign controlled_buffer_1_out = Controller_cp ? controlled_buffer_7_out : 1'bz;  // Controlled_Buffer controlled_buffer_1
  not not_1 (not_1_out, Controller_nlm);
  not not_2 (not_2_out, Controller_nce);
  assign controlled_buffer_2_out[3:0] = Controller_ep ? counter2_1_q0 : 4'bz;  // Controlled_Buffer controlled_buffer_2
  Register___4_bits MAR (
    .X3(controlled_buffer_2_out[3]), .X2(controlled_buffer_2_out[2]), .X1(controlled_buffer_2_out[1]),
    .X0(controlled_buffer_2_out[0]), .Y3(MAR_y0[3]), .Y2(MAR_y0[2]), .Y1(MAR_y0[1]), .Y0(MAR_y0[0]),
    .LOAD(not_1_out), .Clear(CLR), .Clock(controlled_buffer_7_out), .Enable(not_10_out));
  not not_3 (not_3_out, Controller_nei);
  RAM #(.addrWidth(4)) ram_1 (.addr(MAR_y0), .data(controlled_buffer_2_out), .ld(not_2_out));  // open: sel, clk, clr
  not not_4 (not_4_out, Controller_nli);
  Register Ins_Reg (
    .X7(controlled_buffer_2_out[7]), .X6(controlled_buffer_2_out[6]), .X5(controlled_buffer_2_out[5]),
    .X4(controlled_buffer_2_out[4]), .X3(controlled_buffer_2_out[3]), .X2(controlled_buffer_2_out[2]),
    .X1(controlled_buffer_2_out[1]), .X0(controlled_buffer_2_out[0]), .Y7(Ins_Reg_y0[7]), .Y6(Ins_Reg_y0[6]),
    .Y5(Ins_Reg_y0[5]), .Y4(Ins_Reg_y0[4]), .Y3(Ins_Reg_y0[3]), .Y2(Ins_Reg_y0[2]), .Y1(Ins_Reg_y0[1]),
    .Y0(Ins_Reg_y0[0]), .LOAD(not_4_out), .Clear(CLR), .Clock(controlled_buffer_7_out), .Enable(not_10_out));
  Counter2 counter2_1 (
    .CLK(controlled_buffer_1_out), .in_2(CLR), .Q0(counter2_1_q0[0]), .Q1(counter2_1_q0[1]),
    .Q2(counter2_1_q0[2]), .Q3(counter2_1_q0[3]));
  assign controlled_buffer_2_out[3:0] = not_3_out ? Ins_Reg_y0[3:0] : 4'bz;  // Controlled_Buffer controlled_buffer_3
  assign controlled_buffer_2_out = Controller_ea ? Reg_A_y0 : 8'bz;  // Controlled_Buffer controlled_buffer_4
  assign controlled_buffer_2_out = Controller_eu ? ALU_f1 : 8'bz;  // Controlled_Buffer controlled_buffer_5
  not not_5 (not_5_out, Controller_nla);
  Controller Controller (
    .CLK(controlled_buffer_7_out), .CLR(CLR), .l7(Ins_Reg_y0[7]), .l6(Ins_Reg_y0[6]), .l5(Ins_Reg_y0[5]),
    .l4(Ins_Reg_y0[4]), .Cp(Controller_cp), .Ep(Controller_ep), .nLm(Controller_nlm), .nCE(Controller_nce),
    .nLi(Controller_nli), .nEi(Controller_nei), .nLa(Controller_nla), .Ea(Controller_ea), .Su(Controller_su),
    .Eu(Controller_eu), .nLb(Controller_nlb), .nLo(Controller_nlo), .HALT(Controller_halt));
  assign controlled_buffer_6_out = not_8_out ? Reg_B_y0 : 8'bz;  // Controlled_Buffer controlled_buffer_6
  assign controlled_buffer_6_out = Controller_su ? ~Reg_B_y0 : 8'bz;  // Controlled_Inverter controlled_inverter_1
  not not_6 (not_6_out, Controller_nlb);
  not not_7 (not_7_out, Controller_nlo);
  not not_8 (not_8_out, Controller_su);
  not not_9 (not_9_out, Controller_halt);
  assign controlled_buffer_7_out = not_9_out ? Clock_out : 1'bz;  // Controlled_Buffer controlled_buffer_7
  Register Reg_A (
    .X7(controlled_buffer_2_out[7]), .X6(controlled_buffer_2_out[6]), .X5(controlled_buffer_2_out[5]),
    .X4(controlled_buffer_2_out[4]), .X3(controlled_buffer_2_out[3]), .X2(controlled_buffer_2_out[2]),
    .X1(controlled_buffer_2_out[1]), .X0(controlled_buffer_2_out[0]), .Y7(Reg_A_y0[7]), .Y6(Reg_A_y0[6]),
    .Y5(Reg_A_y0[5]), .Y4(Reg_A_y0[4]), .Y3(Reg_A_y0[3]), .Y2(Reg_A_y0[2]), .Y1(Reg_A_y0[1]),
    .Y0(Reg_A_y0[0]), .LOAD(not_5_out), .Clear(CLR), .Clock(controlled_buffer_7_out), .Enable(not_10_out));
  Register Reg_Output (
    .X7(controlled_buffer_2_out[7]), .X6(controlled_buffer_2_out[6]), .X5(controlled_buffer_2_out[5]),
    .X4(controlled_buffer_2_out[4]), .X3(controlled_buffer_2_out[3]), .X2(controlled_buffer_2_out[2]),
    .X1(controlled_buffer_2_out[1]), .X0(controlled_buffer_2_out[0]), .Y7(Reg_Output_y0[7]),
    .Y6(Reg_Output_y0[6]), .Y5(Reg_Output_y0[5]), .Y4(Reg_Output_y0[4]), .Y3(Reg_Output_y0[3]),
    .Y2(Reg_Output_y0[2]), .Y1(Reg_Output_y0[1]), .Y0(Reg_Output_y0[0]), .LOAD(not_7_out), .Clear(CLR),
    .Clock(controlled_buffer_7_out), .Enable(not_10_out));
  not not_10 (not_10_out, in_1);
  Hex_Digit_Display hex_digit_display_1 (.value(Reg_Output_y0[7:4]));  // open: dp
  Clock Clock (.out(Clock_out));
  Hex_Digit_Display hex_digit_display_2 (.value(Reg_Output_y0[3:0]));  // open: dp
  Register Reg_B (
    .X7(controlled_buffer_2_out[7]), .X6(controlled_buffer_2_out[6]), .X5(controlled_buffer_2_out[5]),
    .X4(controlled_buffer_2_out[4]), .X3(controlled_buffer_2_out[3]), .X2(controlled_buffer_2_out[2]),
    .X1(controlled_buffer_2_out[1]), .X0(controlled_buffer_2_out[0]), .Y7(Reg_B_y0[7]), .Y6(Reg_B_y0[6]),
    .Y5(Reg_B_y0[5]), .Y4(Reg_B_y0[4]), .Y3(Reg_B_y0[3]), .Y2(Reg_B_y0[2]), .Y1(Reg_B_y0[1]),
    .Y0(Reg_B_y0[0]), .LOAD(not_6_out), .Clear(CLR), .Clock(controlled_buffer_7_out), .Enable(not_10_out));
  ALU ALU (
    .S1(in_2), .S0(not_10_out), .Cin(Controller_su), .A1(Reg_A_y0[0]), .A2(Reg_A_y0[1]), .A3(Reg_A_y0[2]),
    .A4(Reg_A_y0[3]), .A5(Reg_A_y0[4]), .A6(Reg_A_y0[5]), .A7(Reg_A_y0[6]), .A8(Reg_A_y0[7]),
    .B1(controlled_buffer_6_out[0]), .B2(controlled_buffer_6_out[1]), .B3(controlled_buffer_6_out[2]),
    .B4(controlled_buffer_6_out[3]), .B5(controlled_buffer_6_out[4]), .B6(controlled_buffer_6_out[5]),
    .B7(controlled_buffer_6_out[6]), .B8(controlled_buffer_6_out[7]), .F1(ALU_f1[0]), .F2(ALU_f1[1]),
    .F3(ALU_f1[2]), .F4(ALU_f1[3]), .F5(ALU_f1[4]), .F6(ALU_f1[5]), .F7(ALU_f1[6]), .F8(ALU_f1[7]));

  // Notes on the sheet:
  //   RAM
  //   Reg Ins
  //   MAR
  //   Counter
  //   Controller
  //   Reg A
  //   Reg Output
  //   Reg B
  //   Clock
  //   Enable
  //   Clear
  //   Display
  //   1607014
  //   &
  //   1607021
  //   Input
  //   08 19 2a 2b e0 f0 00 00
  //   0f 0c 05 03 00 00 00 00 
  //   15 + 12 - 5 - 3
  //   ALU
endmodule

module iDecoder (
  input  l6,
  input  l5,
  input  l7,
  input  l4,
  output LDA,
  output ADD,
  output SUB,
  output OUT,
  output HLT
);

  wire and_1_out, and_2_out, and_3_out, and_4_out, and_5_out, not_1_out, not_2_out, not_3_out, not_4_out;

  not not_1 (not_1_out, l7);
  not not_2 (not_2_out, l6);
  not not_3 (not_3_out, l5);
  not not_4 (not_4_out, l4);
  and and_1 (and_1_out, not_1_out, not_2_out, not_3_out, not_4_out);
  and and_2 (and_2_out, not_1_out, not_2_out, not_3_out, l4);
  buf buffer_1 (LDA, and_1_out);
  buf buffer_2 (ADD, and_2_out);
  and and_3 (and_3_out, not_1_out, not_2_out, l5, not_4_out);
  buf buffer_3 (SUB, and_3_out);
  and and_4 (and_4_out, l7, l6, l5, not_4_out);
  and and_5 (and_5_out, l7, l6, l5, l4);
  buf buffer_4 (OUT, and_4_out);
  buf buffer_5 (HLT, and_5_out);

  // Notes on the sheet:
  //   iDecoder
  //   1607014
endmodule

module Register (
  input  X7,
  input  X6,
  input  X5,
  input  X4,
  input  X3,
  input  X2,
  input  X1,
  input  X0,
  input  LOAD,
  input  Clear,
  input  Clock,
  input  Enable,
  output Y7,
  output Y6,
  output Y5,
  output Y4,
  output Y3,
  output Y2,
  output Y1,
  output Y0
);

  wire and_1_out, and_2_out, and_3_out, and_4_out, and_5_out, and_6_out, and_7_out, and_8_out, and_9_out,
       and_10_out, and_11_out, and_12_out, and_13_out, and_14_out, and_15_out, and_16_out, D0_q, D1_q, D2_q,
       D3_q, D4_q, D5_q, D6_q, D7_q, not_1_out, or_1_out, or_2_out, or_3_out, or_4_out, or_5_out, or_6_out,
       or_7_out, or_8_out;

  assign Y7 = Enable ? D7_q : 1'bz;  // Controlled_Buffer controlled_buffer_1
  and and_1 (and_1_out, D7_q, not_1_out);
  D_Flip_Flop D7 (.clk(Clock), .D(or_1_out), .Q(D7_q), .reset(Clear));  // open: Qn, preset, en
  and and_2 (and_2_out, X7, LOAD);
  or or_1 (or_1_out, and_1_out, and_2_out);
  assign Y6 = Enable ? D6_q : 1'bz;  // Controlled_Buffer controlled_buffer_2
  and and_3 (and_3_out, D6_q, not_1_out);
  or or_2 (or_2_out, and_3_out, and_4_out);
  D_Flip_Flop D6 (.clk(Clock), .D(or_2_out), .Q(D6_q), .reset(Clear));  // open: Qn, preset, en
  and and_4 (and_4_out, X6, LOAD);
  assign Y5 = Enable ? D5_q : 1'bz;  // Controlled_Buffer controlled_buffer_3
  and and_5 (and_5_out, D5_q, not_1_out);
  and and_6 (and_6_out, X5, LOAD);
  or or_3 (or_3_out, and_5_out, and_6_out);
  D_Flip_Flop D5 (.clk(Clock), .D(or_3_out), .Q(D5_q), .reset(Clear));  // open: Qn, preset, en
  assign Y4 = Enable ? D4_q : 1'bz;  // Controlled_Buffer controlled_buffer_4
  and and_7 (and_7_out, D4_q, not_1_out);
  or or_4 (or_4_out, and_7_out, and_8_out);
  D_Flip_Flop D4 (.clk(Clock), .D(or_4_out), .Q(D4_q), .reset(Clear));  // open: Qn, preset, en
  and and_8 (and_8_out, X4, LOAD);
  assign Y3 = Enable ? D3_q : 1'bz;  // Controlled_Buffer controlled_buffer_5
  and and_9 (and_9_out, D3_q, not_1_out);
  or or_5 (or_5_out, and_9_out, and_10_out);
  D_Flip_Flop D3 (.clk(Clock), .D(or_5_out), .Q(D3_q), .reset(Clear));  // open: Qn, preset, en
  and and_10 (and_10_out, X3, LOAD);
  assign Y2 = Enable ? D2_q : 1'bz;  // Controlled_Buffer controlled_buffer_6
  and and_11 (and_11_out, D2_q, not_1_out);
  or or_6 (or_6_out, and_11_out, and_12_out);
  D_Flip_Flop D2 (.clk(Clock), .D(or_6_out), .Q(D2_q), .reset(Clear));  // open: Qn, preset, en
  and and_12 (and_12_out, X2, LOAD);
  assign Y1 = Enable ? D1_q : 1'bz;  // Controlled_Buffer controlled_buffer_7
  and and_13 (and_13_out, D1_q, not_1_out);
  D_Flip_Flop D1 (.clk(Clock), .D(or_7_out), .Q(D1_q), .reset(Clear));  // open: Qn, preset, en
  and and_14 (and_14_out, X1, LOAD);
  or or_7 (or_7_out, and_13_out, and_14_out);
  assign Y0 = Enable ? D0_q : 1'bz;  // Controlled_Buffer controlled_buffer_8
  and and_15 (and_15_out, D0_q, not_1_out);
  or or_8 (or_8_out, and_15_out, and_16_out);
  D_Flip_Flop D0 (.clk(Clock), .D(or_8_out), .Q(D0_q), .reset(Clear));  // open: Qn, preset, en
  not not_1 (not_1_out, LOAD);
  and and_16 (and_16_out, X0, LOAD);

  // Notes on the sheet:
  //   1607021
  //   8 bits Register
endmodule

module Register___4_bits (
  input  X3,
  input  X2,
  input  X1,
  input  X0,
  input  LOAD,
  input  Clear,
  input  Clock,
  input  Enable,
  output Y3,
  output Y2,
  output Y1,
  output Y0
);

  wire and_1_out, and_2_out, and_3_out, and_4_out, and_5_out, and_6_out, and_7_out, and_8_out, D0_q, D1_q,
       D2_q, D3_q, not_1_out, or_1_out, or_2_out, or_3_out, or_4_out;

  assign Y3 = Enable ? D3_q : 1'bz;  // Controlled_Buffer controlled_buffer_1
  and and_1 (and_1_out, D3_q, not_1_out);
  or or_1 (or_1_out, and_1_out, and_2_out);
  D_Flip_Flop D3 (.clk(Clock), .D(or_1_out), .Q(D3_q), .reset(Clear));  // open: Qn, preset, en
  and and_2 (and_2_out, X3, LOAD);
  assign Y2 = Enable ? D2_q : 1'bz;  // Controlled_Buffer controlled_buffer_2
  and and_3 (and_3_out, D2_q, not_1_out);
  and and_4 (and_4_out, X2, LOAD);
  or or_2 (or_2_out, and_3_out, and_4_out);
  D_Flip_Flop D2 (.clk(Clock), .D(or_2_out), .Q(D2_q), .reset(Clear));  // open: Qn, preset, en
  assign Y1 = Enable ? D1_q : 1'bz;  // Controlled_Buffer controlled_buffer_3
  and and_5 (and_5_out, D1_q, not_1_out);
  or or_3 (or_3_out, and_5_out, and_6_out);
  D_Flip_Flop D1 (.clk(Clock), .D(or_3_out), .Q(D1_q), .reset(Clear));  // open: Qn, preset, en
  and and_6 (and_6_out, X1, LOAD);
  assign Y0 = Enable ? D0_q : 1'bz;  // Controlled_Buffer controlled_buffer_4
  and and_7 (and_7_out, D0_q, not_1_out);
  or or_4 (or_4_out, and_7_out, and_8_out);
  D_Flip_Flop D0 (.clk(Clock), .D(or_4_out), .Q(D0_q), .reset(Clear));  // open: Qn, preset, en
  not not_1 (not_1_out, LOAD);
  and and_8 (and_8_out, X0, LOAD);

  // Notes on the sheet:
  //   1607021
  //   4 bits Register
endmodule

module Controller (
  input  CLK,
  input  CLR,
  input  l5,
  input  l6,
  input  l7,
  input  l4,
  output Cp,
  output Ep,
  output HALT,
  output nLo,
  output nCE,
  output nLi,
  output nLa,
  output Eu,
  output nLm,
  output nEi,
  output nLb,
  output Ea,
  output Su
);

  wire and_1_out, and_2_out, and_3_out, and_4_out, and_5_out, and_6_out, and_7_out, and_8_out, and_9_out,
       and_10_out, and_11_out, and_12_out, and_14_out, and_16_out, and_17_out, and_18_out, iDecoder_add,
       iDecoder_lda, iDecoder_out, iDecoder_sub, not_2_out, Ring_Counter_t3, Ring_Counter_t4,
       Ring_Counter_t5, Ring_Counter_t6;

  and and_1 (and_1_out, Ring_Counter_t4, iDecoder_lda);
  iDecoder iDecoder (
    .l7(l7), .l6(l6), .l5(l5), .l4(l4), .LDA(iDecoder_lda), .ADD(iDecoder_add), .SUB(iDecoder_sub),
    .OUT(iDecoder_out), .HLT(HALT));
  and and_2 (and_2_out, Ring_Counter_t4, iDecoder_sub);
  and and_3 (and_3_out, Ring_Counter_t4, iDecoder_add);
  nor nor_1 (nLm, and_1_out, and_3_out, and_2_out, Ep);
  and and_4 (and_4_out, Ring_Counter_t5, iDecoder_lda);
  and and_5 (and_5_out, iDecoder_add, Ring_Counter_t5);
  and and_6 (and_6_out, iDecoder_sub, Ring_Counter_t5);
  nor nor_2 (nCE, and_4_out, and_5_out, and_6_out, Ring_Counter_t3);
  not not_1 (nLi, Ring_Counter_t3);
  and and_7 (and_7_out, Ring_Counter_t4, iDecoder_lda);
  and and_8 (and_8_out, Ring_Counter_t4, iDecoder_add);
  and and_9 (and_9_out, Ring_Counter_t4, iDecoder_sub);
  nor nor_3 (nEi, and_7_out, and_8_out, and_9_out);
  and and_10 (and_10_out, iDecoder_add, Ring_Counter_t6);
  and and_11 (and_11_out, Ring_Counter_t5, iDecoder_lda);
  nor nor_4 (nLa, and_11_out, and_10_out, and_12_out);
  and and_12 (and_12_out, iDecoder_sub, Ring_Counter_t6);
  and and_13 (Ea, Ring_Counter_t4, iDecoder_out);
  not not_2 (not_2_out, CLK);
  and and_14 (and_14_out, Ring_Counter_t6, iDecoder_add);
  and and_15 (Su, Ring_Counter_t6, iDecoder_sub);
  and and_16 (and_16_out, Ring_Counter_t6, iDecoder_sub);
  or or_1 (Eu, and_14_out, and_16_out);
  and and_17 (and_17_out, Ring_Counter_t5, iDecoder_add);
  RingCounter Ring_Counter (
    .CLK(not_2_out), .Clear(CLR), .T1(Ep), .T2(Cp), .T3(Ring_Counter_t3), .T4(Ring_Counter_t4),
    .T5(Ring_Counter_t5), .T6(Ring_Counter_t6));
  nand nand_1 (nLo, iDecoder_out, Ring_Counter_t4);
  and and_18 (and_18_out, Ring_Counter_t5, iDecoder_sub);
  nor nor_5 (nLb, and_17_out, and_18_out);

  // Notes on the sheet:
  //   iDecoder
  //   1607014
  //   &
  //   1607021
  //   Controller
  //   Ring Counter
endmodule

module ALU (
  input  S1,
  input  S0,
  input  Cin,
  input  A1,
  input  A2,
  input  A3,
  input  A4,
  input  A5,
  input  A6,
  input  A7,
  input  A8,
  input  B1,
  input  B2,
  input  B3,
  input  B4,
  input  B5,
  input  B6,
  input  B7,
  input  B8,
  output F1,
  output F2,
  output F3,
  output F4,
  output F5,
  output F6,
  output F7,
  output F8
);

  wire fa_1_c, fa_2_c, fa_3_c, fa_4_c, fa_5_c, fa_6_c, fa_7_c, one_zerocircuit_1_y, one_zerocircuit_2_y,
       one_zerocircuit_3_y, one_zerocircuit_4_y, one_zerocircuit_5_y, one_zerocircuit_6_y,
       one_zerocircuit_7_y, one_zerocircuit_8_y;

  One_ZeroCircuit one_zerocircuit_1 (.B(B1), .S0(S0), .S1(S1), .Y(one_zerocircuit_1_y));
  One_ZeroCircuit one_zerocircuit_2 (.B(B2), .S0(S0), .S1(S1), .Y(one_zerocircuit_2_y));
  One_ZeroCircuit one_zerocircuit_3 (.B(B3), .S0(S0), .S1(S1), .Y(one_zerocircuit_3_y));
  One_ZeroCircuit one_zerocircuit_4 (.B(B4), .S0(S0), .S1(S1), .Y(one_zerocircuit_4_y));
  One_ZeroCircuit one_zerocircuit_5 (.B(B5), .S0(S0), .S1(S1), .Y(one_zerocircuit_5_y));
  One_ZeroCircuit one_zerocircuit_6 (.B(B6), .S0(S0), .S1(S1), .Y(one_zerocircuit_6_y));
  One_ZeroCircuit one_zerocircuit_7 (.B(B7), .S0(S0), .S1(S1), .Y(one_zerocircuit_7_y));
  One_ZeroCircuit one_zerocircuit_8 (.B(B8), .S0(S0), .S1(S1), .Y(one_zerocircuit_8_y));
  FA fa_1 (.X(A1), .Y(one_zerocircuit_1_y), .Z(Cin), .S(F1), .C(fa_1_c));
  FA fa_2 (.X(A2), .Y(one_zerocircuit_2_y), .Z(fa_1_c), .S(F2), .C(fa_2_c));
  FA fa_3 (.X(A3), .Y(one_zerocircuit_3_y), .Z(fa_2_c), .S(F3), .C(fa_3_c));
  FA fa_4 (.X(A4), .Y(one_zerocircuit_4_y), .Z(fa_3_c), .S(F4), .C(fa_4_c));
  FA fa_5 (.X(A5), .Y(one_zerocircuit_5_y), .Z(fa_4_c), .S(F5), .C(fa_5_c));
  FA fa_6 (.X(A6), .Y(one_zerocircuit_6_y), .Z(fa_5_c), .S(F6), .C(fa_6_c));
  FA fa_7 (.X(A7), .Y(one_zerocircuit_7_y), .Z(fa_6_c), .S(F7), .C(fa_7_c));
  FA fa_8 (.X(A8), .Y(one_zerocircuit_8_y), .Z(fa_7_c), .S(F8));  // open: C

  // Notes on the sheet:
  //   ALU
  //   1607014
  //   &
  //   1607021
endmodule

module FA (
  input  X,
  input  Y,
  input  Z,
  output S,
  output C
);

  wire and_1_out, and_2_out, xor_1_out;

  xor xor_1 (xor_1_out, X, Y);
  and and_1 (and_1_out, X, Y);
  xor xor_2 (S, xor_1_out, Z);
  and and_2 (and_2_out, xor_1_out, Z);
  or or_1 (C, and_2_out, and_1_out);

  // Notes on the sheet:
  //   1607014
  //   Full Adder
endmodule

module One_ZeroCircuit (
  input  B,
  input  S0,
  input  S1,
  output Y
);

  wire and_1_out, and_2_out, not_1_out;

  not not_1 (not_1_out, B);
  and and_1 (and_1_out, B, S0);
  and and_2 (and_2_out, not_1_out, S1);
  or or_1 (Y, and_1_out, and_2_out);

  // Notes on the sheet:
  //   1607021
  //   One/Zero Circuit
endmodule

module Counter2 (
  input  CLK,
  input  in_2,
  output Q1,
  output Q0,
  output Q2,
  output Q3
);

  wire and_1_out, d_ff_1_qn, d_ff_2_qn, d_ff_3_qn, d_ff_4_qn;

  D_Flip_Flop d_ff_1 (.clk(CLK), .D(d_ff_1_qn), .Q(Q0), .Qn(d_ff_1_qn), .preset(and_1_out), .reset(in_2));  // open: en
  and and_1 (and_1_out, Q1, Q3);
  D_Flip_Flop d_ff_2 (
    .clk(d_ff_1_qn), .D(d_ff_2_qn), .Q(Q1), .Qn(d_ff_2_qn), .preset(and_1_out), .reset(in_2));  // open: en
  D_Flip_Flop d_ff_3 (
    .clk(d_ff_2_qn), .D(d_ff_3_qn), .Q(Q2), .Qn(d_ff_3_qn), .preset(and_1_out), .reset(in_2));  // open: en
  D_Flip_Flop d_ff_4 (
    .clk(d_ff_3_qn), .D(d_ff_4_qn), .Q(Q3), .Qn(d_ff_4_qn), .preset(and_1_out), .reset(in_2));  // open: en

  // Notes on the sheet:
  //   1607014
  //   Counter
endmodule

module RingCounter (
  input  CLK,
  input  Clear,
  output T1,
  output T2,
  output T3,
  output T4,
  output T5,
  output T6
);

  wire nor_1_out;

  nor nor_1 (nor_1_out, T1, T2, T3, T4, T5, T6);
  D_Flip_Flop D1 (.clk(CLK), .D(nor_1_out), .Q(T1), .reset(Clear));  // open: Qn, preset, en
  D_Flip_Flop d_ff_1 (.clk(CLK), .D(T1), .Q(T2), .reset(Clear));  // open: Qn, preset, en
  D_Flip_Flop d_ff_2 (.clk(CLK), .D(T2), .Q(T3), .reset(Clear));  // open: Qn, preset, en
  D_Flip_Flop d_ff_3 (.clk(CLK), .D(T3), .Q(T4), .reset(Clear));  // open: Qn, preset, en
  D_Flip_Flop d_ff_4 (.clk(CLK), .D(T4), .Q(T5), .reset(Clear));  // open: Qn, preset, en
  D_Flip_Flop d_ff_5 (.clk(CLK), .D(T5), .Q(T6), .reset(Clear));  // open: Qn, preset, en

  // Notes on the sheet:
  //   1607021
  //   Ring Counter
endmodule
